// Logisim project warmup.circ as structural Verilog: 1 circuit, main circuit main
module main (
  input  in_1,
  input  in_2,
  input  in_3,
  output out_4,
  output out_5
);

  not not_1 (out_4, in_1);
  and and_1 (out_5, in_2, in_3);
endmodule
