// Logisim project ex1.circ as structural Verilog: 4 circuits, main circuit main
module main (
  output [7:0] non_pipe_out,
  output [7:0] pipe_out
);

  wire CLK_out;
  wire [7:0] Address_Counter_q, rom_1_data;

  Counter Address_Counter (.clk(CLK_out), .Q(Address_Counter_q));  // open: clr, load, up, count, D, carry
  Clock CLK (.out(CLK_out));
  ROM rom_1 (.addr(Address_Counter_q), .data(rom_1_data));
  // Probe on non_pipe_out
  non_pipelined non_pipelined_1 (.in1(rom_1_data[3:0]), .in2(rom_1_data[7:4]), .CLK(CLK_out), .out1(non_pipe_out));
  // Probe on pipe_out
  pipelined pipelined_1 (.in1(rom_1_data[3:0]), .in2(rom_1_data[7:4]), .CLK(CLK_out), .out1(pipe_out));

  // Notes on the sheet:
  //   contents of rom_1 (hex, n*v repeats v):
  //   13 a2 fc 8f 1c 2 b0
endmodule

module non_pipelined (
  input  [3:0] in1,
  input  [3:0] in2,
  input  CLK,
  output [7:0] out1
);

  wire [7:0] move_and_add_1_moved_multiplicand, move_and_add_1_result, move_and_add_2_moved_multiplicand,
       move_and_add_2_result, move_and_add_3_moved_multiplicand, move_and_add_3_result, move_and_add_4_result;

  // Probe on move_and_add_1_result
  move_and_add move_and_add_1 (
    .multiplier(in2[0]), .multiplicand({4'b0000, in1}), .current({8{1'b0}}), .result(move_and_add_1_result),
    .moved_multiplicand(move_and_add_1_moved_multiplicand));
  move_and_add move_and_add_2 (
    .multiplier(in2[1]), .multiplicand(move_and_add_1_moved_multiplicand), .current(move_and_add_1_result),
    .result(move_and_add_2_result), .moved_multiplicand(move_and_add_2_moved_multiplicand));
  move_and_add move_and_add_3 (
    .multiplier(in2[2]), .multiplicand(move_and_add_2_moved_multiplicand), .current(move_and_add_2_result),
    .result(move_and_add_3_result), .moved_multiplicand(move_and_add_3_moved_multiplicand));
  move_and_add move_and_add_4 (
    .multiplier(in2[3]), .multiplicand(move_and_add_3_moved_multiplicand), .current(move_and_add_3_result),
    .result(move_and_add_4_result));  // open: moved_multiplicand
  Register register_1 (.D(move_and_add_4_result), .clk(CLK), .Q(out1));  // open: en, clr
endmodule

module pipelined (
  input  [3:0] in1,
  input  [3:0] in2,
  input  CLK,
  output [7:0] out1
);

  wire register_7_q;
  wire [1:0] register_4_q;
  wire [2:0] register_1_q;
  wire [7:0] move_and_add_1_moved_multiplicand, move_and_add_1_result, move_and_add_2_moved_multiplicand,
       move_and_add_2_result, move_and_add_3_moved_multiplicand, move_and_add_3_result,
       move_and_add_4_moved_multiplicand, move_and_add_4_result, register_2_q, register_3_q, register_5_q,
       register_6_q, register_8_q, register_9_q;

  Register #(.width(3)) register_1 (.D(in2[3:1]), .clk(CLK), .Q(register_1_q));  // open: en, clr
  move_and_add move_and_add_1 (
    .multiplier(in2[0]), .multiplicand({4'b0000, in1}), .current({8{1'b0}}), .result(move_and_add_1_result),
    .moved_multiplicand(move_and_add_1_moved_multiplicand));
  Register register_2 (.D(move_and_add_1_result), .clk(CLK), .Q(register_2_q));  // open: en, clr
  Register register_3 (.D(move_and_add_1_moved_multiplicand), .clk(CLK), .Q(register_3_q));  // open: en, clr
  Register #(.width(2)) register_4 (.D(register_1_q[2:1]), .clk(CLK), .Q(register_4_q));  // open: en, clr
  move_and_add move_and_add_2 (
    .multiplier(register_1_q[0]), .multiplicand(register_3_q), .current(register_2_q),
    .result(move_and_add_2_result), .moved_multiplicand(move_and_add_2_moved_multiplicand));
  Register register_5 (.D(move_and_add_2_result), .clk(CLK), .Q(register_5_q));  // open: en, clr
  Register register_6 (.D(move_and_add_2_moved_multiplicand), .clk(CLK), .Q(register_6_q));  // open: en, clr
  Register #(.width(1)) register_7 (.D(register_4_q[1]), .clk(CLK), .Q(register_7_q));  // open: en, clr
  move_and_add move_and_add_3 (
    .multiplier(register_4_q[0]), .multiplicand(register_6_q), .current(register_5_q),
    .result(move_and_add_3_result), .moved_multiplicand(move_and_add_3_moved_multiplicand));
  Register register_8 (.D(move_and_add_3_result), .clk(CLK), .Q(register_8_q));  // open: en, clr
  Register register_9 (.D(move_and_add_3_moved_multiplicand), .clk(CLK), .Q(register_9_q));  // open: en, clr
  move_and_add move_and_add_4 (
    .multiplier(register_7_q), .multiplicand(register_9_q), .current(register_8_q),
    .result(move_and_add_4_result), .moved_multiplicand(move_and_add_4_moved_multiplicand));
  Register register_10 (.D(move_and_add_4_result), .clk(CLK), .Q(out1));  // open: en, clr
  Register register_11 (.D(move_and_add_4_moved_multiplicand), .clk(CLK));  // open: en, Q, clr

  // Other names for the same wires on the sheet: Clock = CLK
endmodule

module move_and_add (
  input  [7:0] current,
  input  [7:0] multiplicand,
  input  multiplier,
  output [7:0] result,
  output [7:0] moved_multiplicand
);

  wire [7:0] multiplexer_1_out;

  Multiplexer #(.width(8), .enable("false")) multiplexer_1 (
    .in0({8{1'b0}}), .in1(multiplicand), .out(multiplexer_1_out), .sel(multiplier));
  Adder adder_1 (.a(current), .b(multiplexer_1_out), .out(result));  // open: cin, cout
  Shifter shifter_1 (.in(multiplicand), .\dist (3'b001), .out(moved_multiplicand));
endmodule
