// Logisim project alu.circ as structural Verilog: 3 circuits, main circuit alu
module alu (
  input  [31:0] A,
  input  [31:0] B,
  input  [3:0] ALUSel,
  output [31:0] Result
);

  wire [0:0] slt13;
  wire [6:0] cnto15;
  wire [31:0] add3, and0, div9, divu8, mulh7, mulhu6, mult5, or1, remu10, sll14, sra12, srl11, sub4,
       subtractor_1_out, subtractor_2_out, subtractor_3_out, xor2;

  Subtractor #(.width(32)) subtractor_1 (.a(mulhu6), .b(B), .out(subtractor_1_out));  // open: bin, bout
  Subtractor #(.width(32)) subtractor_2 (.a(mulhu6), .b(A), .out(subtractor_2_out));  // open: bin, bout
  assign and0 = A & B;  // AND_Gate and_1, 32 bits wide
  Adder #(.width(32)) adder_1 (.a(A), .b(B), .out(add3));  // open: cin, cout
  Shifter #(.width(32), .shift("lr")) shifter_1 (.in(A), .\dist (B[4:0]), .out(srl11));
  Shifter #(.width(32), .shift("ar")) shifter_2 (.in(A), .\dist (B[4:0]), .out(sra12));
  Shifter #(.width(32)) shifter_3 (.in(A), .\dist (B[4:0]), .out(sll14));
  Subtractor #(.width(32)) subtractor_3 (.a(subtractor_1_out), .b(A), .out(subtractor_3_out));  // open: bin, bout
  Multiplexer #(.select(2), .width(32), .enable("false")) multiplexer_1 (
    .in0(mulhu6), .in1(subtractor_1_out), .in2(subtractor_2_out), .in3(subtractor_3_out), .out(mulh7),
    .sel({B[31], A[31]}));
  assign or1 = A | B;  // OR_Gate or_1, 32 bits wide
  Subtractor #(.width(32)) subtractor_4 (.a(A), .b(B), .out(sub4));  // open: bin, bout
  Comparator #(.width(32)) comparator_1 (.a(A), .b(B), .lt(slt13[0]));  // open: gt, eq
  Multiplier #(.width(32)) multiplier_1 (.a(A), .b(B), .out(mult5), .cout(mulhu6));  // open: cin
  Divider #(.width(32)) divider_1 (.a(A), .b(B), .out(divu8), .rem(remu10));  // open: upper
  signed_div signed_div_1 (.in_1(A), .in_2(B), .out_3(div9));
  assign xor2 = A ^ B;  // XOR_Gate xor_1, 32 bits wide
  BitAdder #(.width(32)) bitadder_1 (.in0(A), .in1(B), .out(cnto15));
  Multiplexer #(.select(4), .width(32), .enable("false")) multiplexer_2 (
    .in0(and0), .in1(or1), .in2(xor2), .in3(add3), .in4(sub4), .in5(mult5), .in6(mulhu6), .in7(mulh7),
    .in8(divu8), .in9(div9), .in10(remu10), .in11(srl11), .in12(sra12), .in13({{31{1'b0}}, slt13[0]}),
    .in14(sll14), .in15({{25{1'b0}}, cnto15}), .out(Result), .sel(ALUSel));

  // Notes on the sheet:
  //   INPUTS to your circuit
  //   DON'T CHANGE THE LOCATIONS OF THE INPUTS AND OUTPUTS!
  //   OUTPUT from your circuit
endmodule

module signed_mul (
  input  [31:0] in_1,
  input  [31:0] in_2,
  output [31:0] out_3,
  output [31:0] out_4
);

  wire [31:0] multiplier_1_cout, multiplier_1_out, multiplier_2_cout, multiplier_2_out, multiplier_3_cout,
       multiplier_3_out, multiplier_4_cout, multiplier_4_out, negator_1_out, negator_2_out, negator_3_out,
       negator_4_out, negator_5_out, negator_6_out, not_1_out, not_2_out;

  Negator #(.width(32)) negator_1 (.in(in_1), .out(negator_1_out));
  Negator #(.width(32)) negator_2 (.in(in_2), .out(negator_2_out));
  Negator #(.width(32)) negator_3 (.in(in_1), .out(negator_3_out));
  Negator #(.width(32)) negator_4 (.in(in_2), .out(negator_4_out));
  Multiplier #(.width(32)) multiplier_1 (
    .a(in_1), .b(in_2), .out(multiplier_1_out), .cout(multiplier_1_cout));  // open: cin
  Multiplier #(.width(32)) multiplier_2 (
    .a(negator_1_out), .b(in_2), .out(multiplier_2_out), .cout(multiplier_2_cout));  // open: cin
  Multiplier #(.width(32)) multiplier_3 (
    .a(in_1), .b(negator_2_out), .out(multiplier_3_out), .cout(multiplier_3_cout));  // open: cin
  Multiplier #(.width(32)) multiplier_4 (
    .a(negator_3_out), .b(negator_4_out), .out(multiplier_4_out), .cout(multiplier_4_cout));  // open: cin
  Negator #(.width(32)) negator_5 (.in(multiplier_2_out), .out(negator_5_out));
  assign not_1_out = ~multiplier_2_cout;  // NOT_Gate not_1, 32 bits wide
  Negator #(.width(32)) negator_6 (.in(multiplier_3_out), .out(negator_6_out));
  assign not_2_out = ~multiplier_3_cout;  // NOT_Gate not_2, 32 bits wide
  Multiplexer #(.select(2), .width(32), .enable("false")) multiplexer_1 (
    .in0(multiplier_1_out), .in1(negator_5_out), .in2(negator_6_out), .in3(multiplier_4_out), .out(out_3),
    .sel({in_2[31], in_1[31]}));
  Multiplexer #(.select(2), .width(32), .enable("false")) multiplexer_2 (
    .in0(multiplier_1_cout), .in1(not_1_out), .in2(not_2_out), .in3(multiplier_4_cout), .out(out_4),
    .sel({in_2[31], in_1[31]}));

  // Other names for the same wires on the sheet: A[31:0] = in_1; B[31:0] = in_2; mluh[31:0] = out_4;
  //   mult[31:0] = out_3; mux[1:0] = {in_2[31], in_1[31]}

  // Notes on the sheet:
  //   INPUTS to your circuit
  //   OUTPUT from your circuit
endmodule

module signed_div (
  input  [31:0] in_1,
  input  [31:0] in_2,
  output [31:0] out_3
);

  wire xor_1_out;
  wire [31:0] divider_1_out, multiplexer_1_out, multiplexer_2_out, negator_1_out, negator_2_out,
       negator_3_out;

  Negator #(.width(32)) negator_1 (.in(in_1), .out(negator_1_out));
  Negator #(.width(32)) negator_2 (.in(in_2), .out(negator_2_out));
  Multiplexer #(.width(32), .enable("false")) multiplexer_1 (
    .in0(in_1), .in1(negator_1_out), .out(multiplexer_1_out), .sel(in_1[31]));
  Multiplexer #(.width(32), .enable("false")) multiplexer_2 (
    .in0(in_2), .in1(negator_2_out), .out(multiplexer_2_out), .sel(in_2[31]));
  Divider #(.width(32)) divider_1 (
    .a(multiplexer_1_out), .b(multiplexer_2_out), .out(divider_1_out));  // open: upper, rem
  xor xor_1 (xor_1_out, in_1[31], in_2[31]);
  Negator #(.width(32)) negator_3 (.in(divider_1_out), .out(negator_3_out));
  Multiplexer #(.width(32), .enable("false")) multiplexer_3 (
    .in0(divider_1_out), .in1(negator_3_out), .out(out_3), .sel(xor_1_out));

  // Other names for the same wires on the sheet: A[31:0] = in_1; B[31:0] = in_2; div[31:0] = out_3

  // Notes on the sheet:
  //   INPUTS to your circuit
  //   OUTPUT from your circuit
endmodule
