// Logisim project cpu.circ as structural Verilog: 4 circuits, main circuit main
module main (
  input  [31:0] INSTRUCTION,
  input  CLOCK,
  output [31:0] FETCH_ADDRESS,
  output [31:0] ra,
  output [31:0] sp,
  output [31:0] t0,
  output [31:0] t1,
  output [31:0] t2,
  output [31:0] s0,
  output [31:0] s1,
  output [31:0] a0
);

  wire BrEq, BrLT, BrUn, BSel, comparator_1_lt, comparator_2_lt, MemRW, PCSel, RegWEn;
  wire [1:0] ASel, WBSel;
  wire [2:0] funct3, Imm_sel;
  wire [3:0] ALUSel;
  wire [6:0] funct7;
  wire [24:0] INST;
  wire [31:0] adder_1_out, adder_2_out, alu_result, bit_extender_1_out, bit_extender_2_out,
       bit_extender_3_out, bit_extender_4_out, bit_extender_5_out, DMEM_readdata, dmem_result, Gen_Imm,
       multiplexer_1_out, multiplexer_2_out, multiplexer_3_out, multiplexer_4_out, PC, R1, R2, register_1_q,
       WriteData;

  Multiplexer #(.select(2), .width(32), .enable("false")) multiplexer_1 (
    .in0(R1), .in1(PC), .in2({32{1'b0}}), .out(multiplexer_1_out), .sel(ASel));  // open: in3
  Multiplexer #(.width(32), .enable("false")) multiplexer_2 (
    .in0(R2), .in1(Gen_Imm), .out(multiplexer_2_out), .sel(BSel));
  Multiplexer #(.width(32), .enable("false")) multiplexer_3 (
    .in0(adder_1_out), .in1(alu_result), .out(multiplexer_3_out), .sel(PCSel));
  Register #(.width(32)) register_1 (.D(multiplexer_3_out), .en(1'b1), .clk(CLOCK), .Q(register_1_q));  // open: clr
  regfile_main RegFile (
    .Read_Register_1_rs1(INST[19:15]), .Read_Register_2_rs2(INST[24:20]), .Write_Register_rd(INST[11:7]),
    .Write_Data(WriteData), .Write_Enable(RegWEn), .Clock(CLOCK), .Read_Data_1(R1), .Read_Data_2(R2),
    .ra(ra), .sp(sp), .t0(t0), .t1(t1), .t2(t2), .s0(s0), .s1(s1), .a0(a0));
  control control_1 (
    .Instruction({funct7, INST[24:15], funct3, INST[11:0]}), .BrEq(BrEq), .BrLT(BrLT), .BrUn(BrUn),
    .ImmSel(Imm_sel), .PCSel(PCSel), .ASel(ASel), .BSel(BSel), .ALUSel(ALUSel), .MemRW(MemRW),
    .RegWEn(RegWEn), .WBSel(WBSel));
  alu Arithmetic_Logic_Unit (.A(multiplexer_1_out), .B(multiplexer_2_out), .ALUSel(ALUSel), .Result(alu_result));
  Adder #(.width(32)) adder_1 (.a(32'h4), .b(register_1_q), .out(adder_1_out));  // open: cin, cout
  Register #(.width(32)) register_2 (.D(register_1_q), .en(1'b1), .clk(CLOCK), .Q(PC));  // open: clr
  Shifter #(.width(32), .shift("lr")) shifter_1 (.in(register_1_q), .\dist (5'b00010), .out(FETCH_ADDRESS));
  Imm_generator imm_generator_1 (.Inst({funct7, INST[24:15], funct3, INST[11:0]}), .Imm_sel(Imm_sel), .Imm(Gen_Imm));
  Multiplexer #(.width(32), .enable("false")) multiplexer_4 (
    .in0(INSTRUCTION), .in1(32'h13), .out(multiplexer_4_out), .sel(PCSel));
  Adder #(.width(32)) adder_2 (.a(PC), .b(32'h4), .out(adder_2_out));  // open: cin, cout
  Comparator #(.width(32)) comparator_1 (.a(R1), .b(R2), .eq(BrEq), .lt(comparator_1_lt));  // open: gt
  Comparator #(.width(32), .mode("unsigned")) comparator_2 (.a(R1), .b(R2), .lt(comparator_2_lt));  // open: gt, eq
  Register #(.width(32)) register_3 (
    .D(multiplexer_4_out), .clk(CLOCK), .Q({funct7, INST[24:15], funct3, INST[11:0]}));  // open: en, clr
  Multiplexer #(.select(2), .width(32), .enable("false")) multiplexer_5 (
    .in0(dmem_result), .in1(alu_result), .in2(adder_2_out), .out(WriteData), .sel(WBSel));  // open: in3
  Multiplexer #(.enable("false")) multiplexer_6 (.in0(comparator_1_lt), .in1(comparator_2_lt), .out(BrLT), .sel(BrUn));
  mem_main DMEM (.WriteAddr(alu_result), .WriteData(R2), .MemRW(MemRW), .ReadData(DMEM_readdata), .clk(CLOCK));
  assign bit_extender_1_out = {{24{DMEM_readdata[7]}}, DMEM_readdata[7:0]};  // Bit_Extender bit_extender_1
  assign bit_extender_2_out = {{16{DMEM_readdata[15]}}, DMEM_readdata[15:0]};  // Bit_Extender bit_extender_2
  Bit_Extender #(.in_width(32), .out_width(32)) bit_extender_3 (.in(DMEM_readdata), .out(bit_extender_3_out));
  assign bit_extender_4_out = {{24{DMEM_readdata[7]}}, DMEM_readdata[7:0]};  // Bit_Extender bit_extender_4
  assign bit_extender_5_out = {{16{DMEM_readdata[15]}}, DMEM_readdata[15:0]};  // Bit_Extender bit_extender_5
  Multiplexer #(.select(3), .width(32), .enable("false")) multiplexer_7 (
    .in0(bit_extender_1_out), .in1(bit_extender_2_out), .in2(bit_extender_3_out), .in3(bit_extender_4_out),
    .in4(bit_extender_5_out), .out(dmem_result), .sel(funct3));  // open: in5, in6, in7

  // Other names for the same wires on the sheet: clk = CLOCK; fetch_addr[31:0] = FETCH_ADDRESS;
  //   Opcode[6:0] = INST[6:0]; INST (some bits) = {funct7, funct3}

  // Notes on the sheet:
  //   Output
  //   Inputs/Outputs from run.circ. DO NOT MOVE THESE.
  //   Inputs
  //   It is OK to move the PC, RegFile, ALU, and MEM to wherever is most convenient for you when constructing your CPU, and to delete this text
  //   2's complement comparator
  //   unsigned comparator
  //   Inputs/Outputs from run.circ. DO NOT MOVE THESE.
endmodule

module Imm_generator (
  input  [31:0] Inst,
  input  [2:0] Imm_sel,
  output [31:0] Imm
);

  wire [31:0] bit_extender_1_out, bit_extender_2_out, bit_extender_3_out, bit_extender_4_out,
       bit_extender_5_out;

  assign bit_extender_1_out = {{20{Inst[31]}}, Inst[31:20]};  // Bit_Extender bit_extender_1
  assign bit_extender_2_out = {{20{Inst[31]}}, {Inst[31:25], Inst[11:7]}};  // Bit_Extender bit_extender_2
  assign bit_extender_3_out = {{19{Inst[31]}}, {Inst[31], Inst[7], Inst[30:25], Inst[11:8], 1'b0}};  // Bit_Extender bit_extender_3
  Bit_Extender #(.in_width(32), .out_width(32)) bit_extender_4 (
    .in({Inst[31:12], {12{1'b0}}}), .out(bit_extender_4_out));
  assign bit_extender_5_out = {{11{Inst[31]}}, {Inst[31], Inst[19:12], Inst[20], Inst[30:21], 1'b0}};  // Bit_Extender bit_extender_5
  Multiplexer #(.select(3), .width(32), .enable("false")) multiplexer_1 (
    .in0(bit_extender_1_out), .in1(bit_extender_2_out), .in2(bit_extender_3_out), .in3(bit_extender_4_out),
    .in4(bit_extender_5_out), .out(Imm), .sel(Imm_sel));  // open: in5, in6, in7

  // Notes on the sheet:
  //   Take away opcode 0-6
  //   I-type
  //   S-type
  //   B-type
  //   U-type
  //   J-type
  //   Imm [11:0]
  //   Imm [4:0] Imm[11:5]
  //   Imm[31:12]
  //   Imm [4:1] Imm [11] Imm[10:5] Imm[12]
  //   Imm[19:12] Imm[11] Imm[10:1] Imm[20]
endmodule

module control (
  input  [31:0] Instruction,
  input  BrEq,
  input  BrLT,
  output BrUn,
  output [2:0] ImmSel,
  output PCSel,
  output [1:0] ASel,
  output BSel,
  output [3:0] ALUSel,
  output MemRW,
  output RegWEn,
  output [1:0] WBSel
);

  wire and_1_out, and_2_out, and_3_out, and_4_out, and_5_out, and_7_out, and_8_out, and_9_out, and_10_out,
       and_11_out, and_12_out, and_13_out, and_14_out, and_15_out, and_16_out, and_17_out, and_18_out,
       and_19_out, BrGT, BrNEq, comparator_1_eq, comparator_2_eq, comparator_3_eq, comparator_4_eq,
       comparator_5_eq, comparator_6_eq, comparator_7_eq, comparator_8_eq, comparator_9_eq, comparator_10_eq,
       comparator_11_eq, comparator_12_eq, comparator_13_eq, comparator_14_eq, comparator_15_eq,
       comparator_16_eq, comparator_17_eq, comparator_18_eq, comparator_19_eq, comparator_29_eq,
       comparator_30_eq, comparator_31_eq, comparator_32_eq, comparator_33_eq, comparator_34_eq,
       comparator_35_eq, comparator_36_eq, comparator_37_eq, comparator_38_eq, comparator_39_eq,
       comparator_40_eq, comparator_41_eq, comparator_42_eq, comparator_43_eq, I_type_03, I_type_13,
       I_type_67, not_5_out, or_1_out, or_2_out, or_4_out, or_5_out, or_6_out, or_7_out, or_8_out, or_9_out,
       R_type, SB_PCSel, SB_type, U_type_17, U_type_37, UJ_type;
  wire [1:0] and_24_out, and_25_out, bit_extender_1_out, bit_extender_5_out, multiplexer_21_out;
  wire [2:0] and_26_out, and_27_out, and_28_out, and_29_out, and_30_out, bit_extender_6_out,
       bit_extender_7_out, bit_extender_8_out, bit_extender_9_out, bit_extender_10_out;
  wire [3:0] and_20_out, and_21_out, and_22_out, bit_extender_2_out, bit_extender_3_out, bit_extender_4_out,
       I_ALUSel, multiplexer_1_out, multiplexer_2_out, multiplexer_3_out, multiplexer_4_out,
       multiplexer_5_out, multiplexer_6_out, multiplexer_7_out, multiplexer_8_out, multiplexer_9_out,
       multiplexer_10_out, multiplexer_11_out, multiplexer_12_out, multiplexer_13_out, multiplexer_14_out,
       multiplexer_15_out, multiplexer_16_out, multiplexer_17_out, multiplexer_18_out, multiplexer_19_out,
       multiplexer_20_out, R_ALUSel;

  not not_1 (BrNEq, BrEq);
  not not_2 (BrGT, BrLT);
  or or_1 (or_1_out, MemRW, SB_type);
  not not_3 (BSel, R_type);
  not not_4 (RegWEn, or_1_out);
  Comparator #(.width(3)) comparator_1 (.a(Instruction[14:12]), .b(3'b000), .eq(comparator_1_eq));  // open: gt, lt
  Comparator #(.width(3)) comparator_2 (.a(Instruction[14:12]), .b(3'b100), .eq(comparator_2_eq));  // open: gt, lt
  Comparator #(.width(3)) comparator_3 (.a(Instruction[14:12]), .b(3'b110), .eq(comparator_3_eq));  // open: gt, lt
  Comparator #(.width(3)) comparator_4 (.a(Instruction[14:12]), .b(3'b001), .eq(comparator_4_eq));  // open: gt, lt
  Comparator #(.width(3)) comparator_5 (.a(Instruction[14:12]), .b(3'b111), .eq(comparator_5_eq));  // open: gt, lt
  Comparator #(.width(3)) comparator_6 (.a(Instruction[14:12]), .b(3'b000), .eq(comparator_6_eq));  // open: gt, lt
  Comparator #(.width(3)) comparator_7 (.a(Instruction[14:12]), .b(3'b001), .eq(comparator_7_eq));  // open: gt, lt
  Comparator #(.width(3)) comparator_8 (.a(Instruction[14:12]), .b(3'b010), .eq(comparator_8_eq));  // open: gt, lt
  Comparator #(.width(3)) comparator_9 (.a(Instruction[14:12]), .b(3'b100), .eq(comparator_9_eq));  // open: gt, lt
  Comparator #(.width(3)) comparator_10 (.a(Instruction[14:12]), .b(3'b101), .eq(comparator_10_eq));  // open: gt, lt
  Comparator #(.width(3)) comparator_11 (.a(Instruction[14:12]), .b(3'b110), .eq(comparator_11_eq));  // open: gt, lt
  Comparator #(.width(3)) comparator_12 (.a(Instruction[14:12]), .b(3'b111), .eq(comparator_12_eq));  // open: gt, lt
  Comparator #(.width(3)) comparator_13 (.a(Instruction[14:12]), .b(3'b000), .eq(comparator_13_eq));  // open: gt, lt
  Comparator #(.width(3)) comparator_14 (.a(Instruction[14:12]), .b(3'b001), .eq(comparator_14_eq));  // open: gt, lt
  Comparator #(.width(3)) comparator_15 (.a(Instruction[14:12]), .b(3'b011), .eq(comparator_15_eq));  // open: gt, lt
  Comparator #(.width(3)) comparator_16 (.a(Instruction[14:12]), .b(3'b100), .eq(comparator_16_eq));  // open: gt, lt
  Comparator #(.width(3)) comparator_17 (.a(Instruction[14:12]), .b(3'b101), .eq(comparator_17_eq));  // open: gt, lt
  Comparator #(.width(3)) comparator_18 (.a(Instruction[14:12]), .b(3'b110), .eq(comparator_18_eq));  // open: gt, lt
  Comparator #(.width(3)) comparator_19 (.a(Instruction[14:12]), .b(3'b111), .eq(comparator_19_eq));  // open: gt, lt
  and and_1 (and_1_out, BrEq, comparator_1_eq);
  and and_2 (and_2_out, BrLT, comparator_2_eq);
  and and_3 (and_3_out, BrLT, comparator_3_eq);
  and and_4 (and_4_out, BrNEq, comparator_4_eq);
  and and_5 (and_5_out, BrGT, comparator_5_eq);
  Multiplexer #(.width(4), .enable("false")) multiplexer_1 (
    .in0(4'b0000), .in1(4'b0011), .out(multiplexer_1_out), .sel(comparator_6_eq));
  Multiplexer #(.width(4), .enable("false")) multiplexer_2 (
    .in0(4'b0000), .in1(4'b1110), .out(multiplexer_2_out), .sel(comparator_7_eq));
  Multiplexer #(.width(4), .enable("false")) multiplexer_3 (
    .in0(4'b0000), .in1(4'b1101), .out(multiplexer_3_out), .sel(comparator_8_eq));
  Multiplexer #(.width(4), .enable("false")) multiplexer_4 (
    .in0(4'b0000), .in1(4'b0010), .out(multiplexer_4_out), .sel(comparator_9_eq));
  Multiplexer #(.width(4), .enable("false")) multiplexer_5 (
    .in0(4'b0000), .in1(4'b1011), .out(multiplexer_5_out), .sel(comparator_10_eq));
  Multiplexer #(.width(4), .enable("false")) multiplexer_6 (
    .in0(4'b0000), .in1(4'b0001), .out(multiplexer_6_out), .sel(comparator_11_eq));
  Multiplexer #(.width(4), .enable("false")) multiplexer_7 (
    .in0(4'b0000), .in1(4'b0000), .out(multiplexer_7_out), .sel(comparator_12_eq));
  Comparator #(.width(7)) comparator_20 (.a(Instruction[6:0]), .b(7'b0110011), .eq(R_type));  // open: gt, lt
  Comparator #(.width(7)) comparator_21 (.a(Instruction[6:0]), .b(7'b0000011), .eq(I_type_03));  // open: gt, lt
  Comparator #(.width(7)) comparator_22 (.a(Instruction[6:0]), .b(7'b0010011), .eq(I_type_13));  // open: gt, lt
  Comparator #(.width(7)) comparator_23 (.a(Instruction[6:0]), .b(7'b0100011), .eq(MemRW));  // open: gt, lt
  Comparator #(.width(7)) comparator_24 (.a(Instruction[6:0]), .b(7'b1100011), .eq(SB_type));  // open: gt, lt
  Comparator #(.width(7)) comparator_25 (.a(Instruction[6:0]), .b(7'b0010111), .eq(U_type_17));  // open: gt, lt
  Comparator #(.width(7)) comparator_26 (.a(Instruction[6:0]), .b(7'b0110111), .eq(U_type_37));  // open: gt, lt
  Comparator #(.width(7)) comparator_27 (.a(Instruction[6:0]), .b(7'b1101111), .eq(UJ_type));  // open: gt, lt
  Comparator #(.width(7)) comparator_28 (.a(Instruction[6:0]), .b(7'b1100111), .eq(I_type_67));  // open: gt, lt
  or or_2 (or_2_out, and_1_out, and_2_out, and_3_out, and_4_out, and_5_out);
  assign I_ALUSel = multiplexer_1_out | multiplexer_2_out | multiplexer_3_out | multiplexer_4_out | multiplexer_5_out | multiplexer_6_out | multiplexer_7_out;  // OR_Gate or_3, 4 bits wide
  Comparator #(.width(7)) comparator_29 (.a(Instruction[31:25]), .b({7{1'b0}}), .eq(comparator_29_eq));  // open: gt, lt
  Comparator #(.width(7)) comparator_30 (
    .a(Instruction[31:25]), .b(7'b0000001), .eq(comparator_30_eq));  // open: gt, lt
  Comparator #(.width(7)) comparator_31 (
    .a(Instruction[31:25]), .b(7'b0100000), .eq(comparator_31_eq));  // open: gt, lt
  Comparator #(.width(7)) comparator_32 (.a(Instruction[31:25]), .b({7{1'b0}}), .eq(comparator_32_eq));  // open: gt, lt
  Comparator #(.width(7)) comparator_33 (
    .a(Instruction[31:25]), .b(7'b0000001), .eq(comparator_33_eq));  // open: gt, lt
  Comparator #(.width(7)) comparator_34 (
    .a(Instruction[31:25]), .b(7'b0000001), .eq(comparator_34_eq));  // open: gt, lt
  Comparator #(.width(7)) comparator_35 (.a(Instruction[31:25]), .b({7{1'b0}}), .eq(comparator_35_eq));  // open: gt, lt
  Comparator #(.width(7)) comparator_36 (
    .a(Instruction[31:25]), .b(7'b0000001), .eq(comparator_36_eq));  // open: gt, lt
  Comparator #(.width(7)) comparator_37 (
    .a(Instruction[31:25]), .b(7'b0000001), .eq(comparator_37_eq));  // open: gt, lt
  Comparator #(.width(7)) comparator_38 (.a(Instruction[31:25]), .b({7{1'b0}}), .eq(comparator_38_eq));  // open: gt, lt
  Comparator #(.width(7)) comparator_39 (.a(Instruction[31:25]), .b({7{1'b0}}), .eq(comparator_39_eq));  // open: gt, lt
  Comparator #(.width(7)) comparator_40 (
    .a(Instruction[31:25]), .b(7'b0000001), .eq(comparator_40_eq));  // open: gt, lt
  Comparator #(.width(7)) comparator_41 (.a(Instruction[31:25]), .b({7{1'b0}}), .eq(comparator_41_eq));  // open: gt, lt
  and and_6 (SB_PCSel, SB_type, or_2_out);
  and and_7 (and_7_out, comparator_13_eq, comparator_29_eq);
  and and_8 (and_8_out, comparator_13_eq, comparator_30_eq);
  and and_9 (and_9_out, comparator_13_eq, comparator_31_eq);
  and and_10 (and_10_out, comparator_14_eq, comparator_32_eq);
  and and_11 (and_11_out, comparator_14_eq, comparator_33_eq);
  and and_12 (and_12_out, comparator_15_eq, comparator_34_eq);
  and and_13 (and_13_out, comparator_16_eq, comparator_35_eq);
  and and_14 (and_14_out, comparator_16_eq, comparator_36_eq);
  and and_15 (and_15_out, comparator_17_eq, comparator_37_eq);
  and and_16 (and_16_out, comparator_17_eq, comparator_38_eq);
  and and_17 (and_17_out, comparator_18_eq, comparator_39_eq);
  and and_18 (and_18_out, comparator_19_eq, comparator_40_eq);
  and and_19 (and_19_out, comparator_19_eq, comparator_41_eq);
  or or_4 (or_4_out, I_type_13, R_type);
  Multiplexer #(.width(4), .enable("false")) multiplexer_8 (
    .in0(4'b0000), .in1(4'b0011), .out(multiplexer_8_out), .sel(and_7_out));
  Multiplexer #(.width(4), .enable("false")) multiplexer_9 (
    .in0(4'b0000), .in1(4'b0101), .out(multiplexer_9_out), .sel(and_8_out));
  Multiplexer #(.width(4), .enable("false")) multiplexer_10 (
    .in0(4'b0000), .in1(4'b0100), .out(multiplexer_10_out), .sel(and_9_out));
  Multiplexer #(.width(4), .enable("false")) multiplexer_11 (
    .in0(4'b0000), .in1(4'b1110), .out(multiplexer_11_out), .sel(and_10_out));
  Multiplexer #(.width(4), .enable("false")) multiplexer_12 (
    .in0(4'b0000), .in1(4'b0111), .out(multiplexer_12_out), .sel(and_11_out));
  Multiplexer #(.width(4), .enable("false")) multiplexer_13 (
    .in0(4'b0000), .in1(4'b0110), .out(multiplexer_13_out), .sel(and_12_out));
  Multiplexer #(.width(4), .enable("false")) multiplexer_14 (
    .in0(4'b0000), .in1(4'b0010), .out(multiplexer_14_out), .sel(and_13_out));
  Multiplexer #(.width(4), .enable("false")) multiplexer_15 (
    .in0(4'b0000), .in1(4'b1001), .out(multiplexer_15_out), .sel(and_14_out));
  Multiplexer #(.width(4), .enable("false")) multiplexer_16 (
    .in0(4'b0000), .in1(4'b1000), .out(multiplexer_16_out), .sel(and_15_out));
  Multiplexer #(.width(4), .enable("false")) multiplexer_17 (
    .in0(4'b0000), .in1(4'b1011), .out(multiplexer_17_out), .sel(and_16_out));
  Multiplexer #(.width(4), .enable("false")) multiplexer_18 (
    .in0(4'b0000), .in1(4'b0001), .out(multiplexer_18_out), .sel(and_17_out));
  Multiplexer #(.width(4), .enable("false")) multiplexer_19 (
    .in0(4'b0000), .in1(4'b1010), .out(multiplexer_19_out), .sel(and_18_out));
  Multiplexer #(.width(4), .enable("false")) multiplexer_20 (
    .in0(4'b0000), .in1(4'b0000), .out(multiplexer_20_out), .sel(and_19_out));
  Comparator #(.width(3)) comparator_42 (.a(Instruction[14:12]), .b(3'b110), .eq(comparator_42_eq));  // open: gt, lt
  Comparator #(.width(3)) comparator_43 (.a(Instruction[14:12]), .b(3'b111), .eq(comparator_43_eq));  // open: gt, lt
  or or_5 (or_5_out, SB_type, U_type_17, UJ_type);
  assign bit_extender_1_out = {{1{or_5_out}}, or_5_out};  // Bit_Extender bit_extender_1
  or or_6 (or_6_out, I_type_03, I_type_13, I_type_67);
  or or_7 (or_7_out, U_type_17, U_type_37);
  not not_5 (not_5_out, or_4_out);
  assign bit_extender_2_out = {{3{not_5_out}}, not_5_out};  // Bit_Extender bit_extender_2
  assign bit_extender_3_out = {{3{R_type}}, R_type};  // Bit_Extender bit_extender_3
  assign bit_extender_4_out = {{3{I_type_13}}, I_type_13};  // Bit_Extender bit_extender_4
  or or_8 (or_8_out, comparator_42_eq, comparator_43_eq);
  assign bit_extender_5_out = {{1{U_type_37}}, U_type_37};  // Bit_Extender bit_extender_5
  or or_9 (or_9_out, R_type, I_type_13, U_type_17, U_type_37);
  assign bit_extender_6_out = {{2{or_6_out}}, or_6_out};  // Bit_Extender bit_extender_6
  assign bit_extender_7_out = {{2{MemRW}}, MemRW};  // Bit_Extender bit_extender_7
  assign bit_extender_8_out = {{2{SB_type}}, SB_type};  // Bit_Extender bit_extender_8
  assign bit_extender_9_out = {{2{or_7_out}}, or_7_out};  // Bit_Extender bit_extender_9
  assign bit_extender_10_out = {{2{UJ_type}}, UJ_type};  // Bit_Extender bit_extender_10
  assign and_20_out = 4'b0011 & bit_extender_2_out;  // AND_Gate and_20, 4 bits wide
  assign and_21_out = R_ALUSel & bit_extender_3_out;  // AND_Gate and_21, 4 bits wide
  assign and_22_out = I_ALUSel & bit_extender_4_out;  // AND_Gate and_22, 4 bits wide
  assign R_ALUSel = multiplexer_8_out | multiplexer_9_out | multiplexer_10_out | multiplexer_11_out | multiplexer_12_out | multiplexer_13_out | multiplexer_14_out | multiplexer_15_out | multiplexer_16_out | multiplexer_17_out | multiplexer_18_out | multiplexer_19_out | multiplexer_20_out;  // OR_Gate or_10, 4 bits wide
  and and_23 (BrUn, SB_type, or_8_out);
  assign and_24_out = bit_extender_1_out & 2'b01;  // AND_Gate and_24, 2 bits wide
  assign and_25_out = bit_extender_5_out & 2'b10;  // AND_Gate and_25, 2 bits wide
  Multiplexer #(.width(2), .enable("false")) multiplexer_21 (
    .in0(2'b10), .in1(2'b01), .out(multiplexer_21_out), .sel(or_9_out));
  assign and_26_out = bit_extender_6_out & 3'b000;  // AND_Gate and_26, 3 bits wide
  assign and_27_out = bit_extender_7_out & 3'b001;  // AND_Gate and_27, 3 bits wide
  assign and_28_out = bit_extender_8_out & 3'b010;  // AND_Gate and_28, 3 bits wide
  assign and_29_out = bit_extender_9_out & 3'b011;  // AND_Gate and_29, 3 bits wide
  assign and_30_out = bit_extender_10_out & 3'b100;  // AND_Gate and_30, 3 bits wide
  assign ALUSel = and_20_out | and_21_out | and_22_out;  // OR_Gate or_11, 4 bits wide
  or or_12 (PCSel, SB_PCSel, UJ_type, I_type_67);
  assign ASel = and_24_out | and_25_out;  // OR_Gate or_13, 2 bits wide
  Multiplexer #(.width(2), .enable("false")) multiplexer_22 (
    .in0(multiplexer_21_out), .in1(2'b00), .out(WBSel), .sel(I_type_03));
  assign ImmSel = and_26_out | and_27_out | and_28_out | and_29_out | and_30_out;  // OR_Gate or_14, 3 bits wide

  // Other names for the same wires on the sheet: INST[31:0] = Instruction; Opcode[6:0] = Instruction[6:0];
  //   funct3[2:0] = Instruction[14:12]; funct7[6:0] = Instruction[31:25]; S_type = MemRW
endmodule

module control_abandon (
  input  [31:0] in_1,
  input  in_2,
  input  in_3,
  output out_4,
  output [2:0] out_5,
  output out_6,
  output [1:0] out_7,
  output out_8,
  output [3:0] out_9,
  output out_10,
  output out_11,
  output [1:0] out_12
);

  wire and_1_out, and_2_out, and_3_out, and_4_out, and_5_out, and_6_out, and_7_out, and_8_out, and_9_out,
       and_10_out, and_11_out, and_12_out, and_13_out, and_14_out, and_15_out, and_16_out, and_17_out,
       and_18_out, and_19_out, and_20_out, and_21_out, and_22_out, and_23_out, and_24_out, and_25_out,
       and_26_out, and_27_out, and_28_out, and_29_out, and_30_out, and_31_out, and_32_out, and_33_out,
       and_34_out, and_35_out, and_36_out, and_37_out, comparator_1_eq, comparator_2_eq, comparator_3_eq,
       comparator_4_eq, comparator_5_eq, comparator_6_eq, comparator_7_eq, comparator_8_eq, comparator_9_eq,
       comparator_10_eq, comparator_11_eq, comparator_12_eq, comparator_13_eq, comparator_14_eq,
       comparator_15_eq, comparator_16_eq, comparator_17_eq, comparator_18_eq, comparator_19_eq,
       comparator_20_eq, comparator_21_eq, comparator_22_eq, comparator_23_eq, comparator_24_eq,
       comparator_25_eq, comparator_26_eq, comparator_27_eq, comparator_28_eq, comparator_29_eq,
       comparator_30_eq, comparator_31_eq, comparator_32_eq, comparator_33_eq, comparator_34_eq,
       comparator_35_eq, comparator_36_eq, comparator_37_eq, comparator_38_eq, comparator_39_eq,
       comparator_40_eq, comparator_41_eq, comparator_42_eq, comparator_43_eq, comparator_44_eq,
       comparator_45_eq, comparator_46_eq, comparator_47_eq, comparator_48_eq, comparator_49_eq,
       comparator_50_eq, comparator_51_eq, comparator_52_eq, comparator_53_eq, comparator_54_eq,
       comparator_55_eq, comparator_56_eq, comparator_57_eq, comparator_58_eq, comparator_59_eq,
       comparator_60_eq, comparator_61_eq, comparator_62_eq, comparator_63_eq, comparator_64_eq,
       comparator_65_eq, comparator_66_eq, comparator_67_eq, comparator_68_eq, comparator_69_eq,
       comparator_70_eq, comparator_71_eq, comparator_72_eq, comparator_73_eq, comparator_74_eq,
       comparator_75_eq, comparator_76_eq, comparator_77_eq, comparator_78_eq, comparator_79_eq,
       comparator_80_eq, comparator_81_eq, comparator_82_eq, comparator_83_eq, comparator_84_eq,
       comparator_85_eq, comparator_86_eq, comparator_87_eq, comparator_88_eq, comparator_89_eq,
       comparator_90_eq, comparator_91_eq, comparator_92_eq, comparator_93_eq, comparator_94_eq, not_1_out,
       not_2_out, not_3_out, not_4_out;
  wire [5:0] add, addi, and_c641ead7, andi, auipc, beq, beq2, bgeu, bgeu2, blt, blt2, bltu, bltu2, bne, bne2,
       div, divu, jal, jalr, lb, lbu, lh, lhu, lui, mul, mulh, mulhu, or_2_out, or_13e46807, ori, remu,
       sll_541af34d, slli, slti, srl_c9755298, srli, sub, sw, xor_aa50a71f, xori;
  wire [13:7] rom_1_data;

  Comparator #(.width(7), .mode("unsigned")) comparator_1 (
    .a(in_1[6:0]), .b(7'b0110011), .eq(comparator_1_eq));  // open: gt, lt
  Comparator #(.width(3), .mode("unsigned")) comparator_2 (
    .a(in_1[14:12]), .b(3'b000), .eq(comparator_2_eq));  // open: gt, lt
  Comparator #(.width(7), .mode("unsigned")) comparator_3 (
    .a(in_1[31:25]), .b({7{1'b0}}), .eq(comparator_3_eq));  // open: gt, lt
  Comparator #(.width(7), .mode("unsigned")) comparator_4 (
    .a(in_1[6:0]), .b(7'b0110011), .eq(comparator_4_eq));  // open: gt, lt
  Comparator #(.width(3), .mode("unsigned")) comparator_5 (
    .a(in_1[14:12]), .b(3'b000), .eq(comparator_5_eq));  // open: gt, lt
  Comparator #(.width(7), .mode("unsigned")) comparator_6 (
    .a(in_1[31:25]), .b(7'b0000001), .eq(comparator_6_eq));  // open: gt, lt
  Comparator #(.width(7), .mode("unsigned")) comparator_7 (
    .a(in_1[6:0]), .b(7'b0110011), .eq(comparator_7_eq));  // open: gt, lt
  Comparator #(.width(3), .mode("unsigned")) comparator_8 (
    .a(in_1[14:12]), .b(3'b000), .eq(comparator_8_eq));  // open: gt, lt
  Comparator #(.width(7), .mode("unsigned")) comparator_9 (
    .a(in_1[31:25]), .b(7'b0100000), .eq(comparator_9_eq));  // open: gt, lt
  Comparator #(.width(7), .mode("unsigned")) comparator_10 (
    .a(in_1[6:0]), .b(7'b0110011), .eq(comparator_10_eq));  // open: gt, lt
  Comparator #(.width(3), .mode("unsigned")) comparator_11 (
    .a(in_1[14:12]), .b(3'b001), .eq(comparator_11_eq));  // open: gt, lt
  Comparator #(.width(7), .mode("unsigned")) comparator_12 (
    .a(in_1[31:25]), .b({7{1'b0}}), .eq(comparator_12_eq));  // open: gt, lt
  Comparator #(.width(7), .mode("unsigned")) comparator_13 (
    .a(in_1[6:0]), .b(7'b0110011), .eq(comparator_13_eq));  // open: gt, lt
  Comparator #(.width(3), .mode("unsigned")) comparator_14 (
    .a(in_1[14:12]), .b(3'b001), .eq(comparator_14_eq));  // open: gt, lt
  Comparator #(.width(7), .mode("unsigned")) comparator_15 (
    .a(in_1[31:25]), .b(7'b0000001), .eq(comparator_15_eq));  // open: gt, lt
  Comparator #(.width(7), .mode("unsigned")) comparator_16 (
    .a(in_1[6:0]), .b(7'b0110011), .eq(comparator_16_eq));  // open: gt, lt
  Comparator #(.width(3), .mode("unsigned")) comparator_17 (
    .a(in_1[14:12]), .b(3'b011), .eq(comparator_17_eq));  // open: gt, lt
  Comparator #(.width(7), .mode("unsigned")) comparator_18 (
    .a(in_1[31:25]), .b(7'b0000001), .eq(comparator_18_eq));  // open: gt, lt
  Comparator #(.width(7), .mode("unsigned")) comparator_19 (
    .a(in_1[6:0]), .b(7'b0110011), .eq(comparator_19_eq));  // open: gt, lt
  Comparator #(.width(3), .mode("unsigned")) comparator_20 (
    .a(in_1[14:12]), .b(3'b100), .eq(comparator_20_eq));  // open: gt, lt
  Comparator #(.width(7), .mode("unsigned")) comparator_21 (
    .a(in_1[31:25]), .b({7{1'b0}}), .eq(comparator_21_eq));  // open: gt, lt
  Comparator #(.width(7), .mode("unsigned")) comparator_22 (
    .a(in_1[6:0]), .b(7'b0110011), .eq(comparator_22_eq));  // open: gt, lt
  Comparator #(.width(3), .mode("unsigned")) comparator_23 (
    .a(in_1[14:12]), .b(3'b100), .eq(comparator_23_eq));  // open: gt, lt
  Comparator #(.width(7), .mode("unsigned")) comparator_24 (
    .a(in_1[31:25]), .b(7'b0000001), .eq(comparator_24_eq));  // open: gt, lt
  Comparator #(.width(7), .mode("unsigned")) comparator_25 (
    .a(in_1[6:0]), .b(7'b0110011), .eq(comparator_25_eq));  // open: gt, lt
  Comparator #(.width(3), .mode("unsigned")) comparator_26 (
    .a(in_1[14:12]), .b(3'b101), .eq(comparator_26_eq));  // open: gt, lt
  Comparator #(.width(7), .mode("unsigned")) comparator_27 (
    .a(in_1[31:25]), .b(7'b0000001), .eq(comparator_27_eq));  // open: gt, lt
  Comparator #(.width(7), .mode("unsigned")) comparator_28 (
    .a(in_1[6:0]), .b(7'b0110011), .eq(comparator_28_eq));  // open: gt, lt
  Comparator #(.width(3), .mode("unsigned")) comparator_29 (
    .a(in_1[14:12]), .b(3'b101), .eq(comparator_29_eq));  // open: gt, lt
  Comparator #(.width(7), .mode("unsigned")) comparator_30 (
    .a(in_1[31:25]), .b({7{1'b0}}), .eq(comparator_30_eq));  // open: gt, lt
  Comparator #(.width(7), .mode("unsigned")) comparator_31 (
    .a(in_1[6:0]), .b(7'b0110011), .eq(comparator_31_eq));  // open: gt, lt
  Comparator #(.width(3), .mode("unsigned")) comparator_32 (
    .a(in_1[14:12]), .b(3'b110), .eq(comparator_32_eq));  // open: gt, lt
  Comparator #(.width(7), .mode("unsigned")) comparator_33 (
    .a(in_1[31:25]), .b({7{1'b0}}), .eq(comparator_33_eq));  // open: gt, lt
  Comparator #(.width(7), .mode("unsigned")) comparator_34 (
    .a(in_1[6:0]), .b(7'b0110011), .eq(comparator_34_eq));  // open: gt, lt
  Comparator #(.width(3), .mode("unsigned")) comparator_35 (
    .a(in_1[14:12]), .b(3'b111), .eq(comparator_35_eq));  // open: gt, lt
  Comparator #(.width(7), .mode("unsigned")) comparator_36 (
    .a(in_1[31:25]), .b(7'b0000001), .eq(comparator_36_eq));  // open: gt, lt
  Comparator #(.width(7), .mode("unsigned")) comparator_37 (
    .a(in_1[6:0]), .b(7'b0110011), .eq(comparator_37_eq));  // open: gt, lt
  Comparator #(.width(3), .mode("unsigned")) comparator_38 (
    .a(in_1[14:12]), .b(3'b111), .eq(comparator_38_eq));  // open: gt, lt
  Comparator #(.width(7), .mode("unsigned")) comparator_39 (
    .a(in_1[31:25]), .b({7{1'b0}}), .eq(comparator_39_eq));  // open: gt, lt
  and and_1 (and_1_out, comparator_1_eq, comparator_2_eq, comparator_3_eq);
  and and_2 (and_2_out, comparator_4_eq, comparator_5_eq, comparator_6_eq);
  and and_3 (and_3_out, comparator_7_eq, comparator_8_eq, comparator_9_eq);
  and and_4 (and_4_out, comparator_10_eq, comparator_11_eq, comparator_12_eq);
  and and_5 (and_5_out, comparator_13_eq, comparator_14_eq, comparator_15_eq);
  and and_6 (and_6_out, comparator_16_eq, comparator_17_eq, comparator_18_eq);
  and and_7 (and_7_out, comparator_19_eq, comparator_20_eq, comparator_21_eq);
  and and_8 (and_8_out, comparator_22_eq, comparator_23_eq, comparator_24_eq);
  and and_9 (and_9_out, comparator_25_eq, comparator_26_eq, comparator_27_eq);
  and and_10 (and_10_out, comparator_28_eq, comparator_29_eq, comparator_30_eq);
  and and_11 (and_11_out, comparator_31_eq, comparator_32_eq, comparator_33_eq);
  and and_12 (and_12_out, comparator_34_eq, comparator_35_eq, comparator_36_eq);
  and and_13 (and_13_out, comparator_37_eq, comparator_38_eq, comparator_39_eq);
  Multiplexer #(.width(6), .enable("false")) multiplexer_1 (
    .in0({6{1'b0}}), .in1(6'b000001), .out(add), .sel(and_1_out));
  Multiplexer #(.width(6), .enable("false")) multiplexer_2 (
    .in0({6{1'b0}}), .in1(6'b000010), .out(mul), .sel(and_2_out));
  Multiplexer #(.width(6), .enable("false")) multiplexer_3 (
    .in0({6{1'b0}}), .in1(6'b000011), .out(sub), .sel(and_3_out));
  Multiplexer #(.width(6), .enable("false")) multiplexer_4 (
    .in0({6{1'b0}}), .in1(6'b000100), .out(sll_541af34d), .sel(and_4_out));
  Multiplexer #(.width(6), .enable("false")) multiplexer_5 (
    .in0({6{1'b0}}), .in1(6'b000101), .out(mulh), .sel(and_5_out));
  Multiplexer #(.width(6), .enable("false")) multiplexer_6 (
    .in0({6{1'b0}}), .in1(6'b000110), .out(mulhu), .sel(and_6_out));
  Multiplexer #(.width(6), .enable("false")) multiplexer_7 (
    .in0({6{1'b0}}), .in1(6'b000111), .out(xor_aa50a71f), .sel(and_7_out));
  Multiplexer #(.width(6), .enable("false")) multiplexer_8 (
    .in0({6{1'b0}}), .in1(6'b001000), .out(div), .sel(and_8_out));
  Multiplexer #(.width(6), .enable("false")) multiplexer_9 (
    .in0({6{1'b0}}), .in1(6'b001001), .out(divu), .sel(and_9_out));
  Multiplexer #(.width(6), .enable("false")) multiplexer_10 (
    .in0({6{1'b0}}), .in1(6'b001010), .out(srl_c9755298), .sel(and_10_out));
  Multiplexer #(.width(6), .enable("false")) multiplexer_11 (
    .in0({6{1'b0}}), .in1(6'b001011), .out(or_13e46807), .sel(and_11_out));
  Multiplexer #(.width(6), .enable("false")) multiplexer_12 (
    .in0({6{1'b0}}), .in1(6'b001100), .out(remu), .sel(and_12_out));
  Multiplexer #(.width(6), .enable("false")) multiplexer_13 (
    .in0({6{1'b0}}), .in1(6'b001101), .out(and_c641ead7), .sel(and_13_out));
  Comparator #(.width(7), .mode("unsigned")) comparator_40 (
    .a(in_1[6:0]), .b(7'b0000011), .eq(comparator_40_eq));  // open: gt, lt
  Comparator #(.width(3), .mode("unsigned")) comparator_41 (
    .a(in_1[14:12]), .b(3'b000), .eq(comparator_41_eq));  // open: gt, lt
  Comparator #(.width(7), .mode("unsigned")) comparator_42 (
    .a(in_1[6:0]), .b(7'b0000011), .eq(comparator_42_eq));  // open: gt, lt
  Comparator #(.width(3), .mode("unsigned")) comparator_43 (
    .a(in_1[14:12]), .b(3'b001), .eq(comparator_43_eq));  // open: gt, lt
  Comparator #(.width(7), .mode("unsigned")) comparator_44 (
    .a(in_1[6:0]), .b(7'b0000011), .eq(comparator_44_eq));  // open: gt, lt
  Comparator #(.width(3), .mode("unsigned")) comparator_45 (
    .a(in_1[14:12]), .b(3'b010), .eq(comparator_45_eq));  // open: gt, lt
  Comparator #(.width(7), .mode("unsigned")) comparator_46 (
    .a(in_1[6:0]), .b(7'b0000011), .eq(comparator_46_eq));  // open: gt, lt
  Comparator #(.width(3), .mode("unsigned")) comparator_47 (
    .a(in_1[14:12]), .b(3'b100), .eq(comparator_47_eq));  // open: gt, lt
  Comparator #(.width(7), .mode("unsigned")) comparator_48 (
    .a(in_1[6:0]), .b(7'b0000011), .eq(comparator_48_eq));  // open: gt, lt
  Comparator #(.width(3), .mode("unsigned")) comparator_49 (
    .a(in_1[14:12]), .b(3'b101), .eq(comparator_49_eq));  // open: gt, lt
  Comparator #(.width(7), .mode("unsigned")) comparator_50 (
    .a(in_1[6:0]), .b(7'b0010011), .eq(comparator_50_eq));  // open: gt, lt
  Comparator #(.width(3), .mode("unsigned")) comparator_51 (
    .a(in_1[14:12]), .b(3'b000), .eq(comparator_51_eq));  // open: gt, lt
  Comparator #(.width(7), .mode("unsigned")) comparator_52 (
    .a(in_1[6:0]), .b(7'b0010011), .eq(comparator_52_eq));  // open: gt, lt
  Comparator #(.width(3), .mode("unsigned")) comparator_53 (
    .a(in_1[14:12]), .b(3'b001), .eq(comparator_53_eq));  // open: gt, lt
  Comparator #(.width(7), .mode("unsigned")) comparator_54 (
    .a(in_1[31:25]), .b({7{1'b0}}), .eq(comparator_54_eq));  // open: gt, lt
  Comparator #(.width(7), .mode("unsigned")) comparator_55 (
    .a(in_1[6:0]), .b(7'b0010011), .eq(comparator_55_eq));  // open: gt, lt
  Comparator #(.width(3), .mode("unsigned")) comparator_56 (
    .a(in_1[14:12]), .b(3'b010), .eq(comparator_56_eq));  // open: gt, lt
  Comparator #(.width(7), .mode("unsigned")) comparator_57 (
    .a(in_1[6:0]), .b(7'b0010011), .eq(comparator_57_eq));  // open: gt, lt
  Comparator #(.width(3), .mode("unsigned")) comparator_58 (
    .a(in_1[14:12]), .b(3'b100), .eq(comparator_58_eq));  // open: gt, lt
  Comparator #(.width(7), .mode("unsigned")) comparator_59 (
    .a(in_1[6:0]), .b(7'b0010011), .eq(comparator_59_eq));  // open: gt, lt
  Comparator #(.width(3), .mode("unsigned")) comparator_60 (
    .a(in_1[14:12]), .b(3'b101), .eq(comparator_60_eq));  // open: gt, lt
  Comparator #(.width(7), .mode("unsigned")) comparator_61 (
    .a(in_1[31:25]), .b({7{1'b0}}), .eq(comparator_61_eq));  // open: gt, lt
  Comparator #(.width(7), .mode("unsigned")) comparator_62 (
    .a(in_1[6:0]), .b(7'b0010011), .eq(comparator_62_eq));  // open: gt, lt
  Comparator #(.width(3), .mode("unsigned")) comparator_63 (
    .a(in_1[14:12]), .b(3'b110), .eq(comparator_63_eq));  // open: gt, lt
  Comparator #(.width(7), .mode("unsigned")) comparator_64 (
    .a(in_1[6:0]), .b(7'b0010011), .eq(comparator_64_eq));  // open: gt, lt
  Comparator #(.width(3), .mode("unsigned")) comparator_65 (
    .a(in_1[14:12]), .b(3'b111), .eq(comparator_65_eq));  // open: gt, lt
  and and_14 (and_14_out, comparator_40_eq, comparator_41_eq);
  and and_15 (and_15_out, comparator_42_eq, comparator_43_eq);
  and and_16 (and_16_out, comparator_44_eq, comparator_45_eq);
  and and_17 (and_17_out, comparator_46_eq, comparator_47_eq);
  and and_18 (and_18_out, comparator_48_eq, comparator_49_eq);
  and and_19 (and_19_out, comparator_50_eq, comparator_51_eq);
  and and_20 (and_20_out, comparator_52_eq, comparator_53_eq, comparator_54_eq);
  and and_21 (and_21_out, comparator_55_eq, comparator_56_eq);
  and and_22 (and_22_out, comparator_57_eq, comparator_58_eq);
  and and_23 (and_23_out, comparator_59_eq, comparator_60_eq, comparator_61_eq);
  and and_24 (and_24_out, comparator_62_eq, comparator_63_eq);
  and and_25 (and_25_out, comparator_64_eq, comparator_65_eq);
  Multiplexer #(.width(6), .enable("false")) multiplexer_14 (
    .in0({6{1'b0}}), .in1(6'b001110), .out(lb), .sel(and_14_out));
  Multiplexer #(.width(6), .enable("false")) multiplexer_15 (
    .in0({6{1'b0}}), .in1(6'b001111), .out(lh), .sel(and_15_out));
  Multiplexer #(.width(6), .enable("false")) multiplexer_16 (
    .in0({6{1'b0}}), .in1(6'b010000), .out(lb), .sel(and_16_out));
  Multiplexer #(.width(6), .enable("false")) multiplexer_17 (
    .in0({6{1'b0}}), .in1(6'b010001), .out(lbu), .sel(and_17_out));
  Multiplexer #(.width(6), .enable("false")) multiplexer_18 (
    .in0({6{1'b0}}), .in1(6'b010010), .out(lhu), .sel(and_18_out));
  Multiplexer #(.width(6), .enable("false")) multiplexer_19 (
    .in0({6{1'b0}}), .in1(6'b010011), .out(addi), .sel(and_19_out));
  Multiplexer #(.width(6), .enable("false")) multiplexer_20 (
    .in0({6{1'b0}}), .in1(6'b010100), .out(slli), .sel(and_20_out));
  Multiplexer #(.width(6), .enable("false")) multiplexer_21 (
    .in0({6{1'b0}}), .in1(6'b010101), .out(slti), .sel(and_21_out));
  Multiplexer #(.width(6), .enable("false")) multiplexer_22 (
    .in0({6{1'b0}}), .in1(6'b010110), .out(xori), .sel(and_22_out));
  Multiplexer #(.width(6), .enable("false")) multiplexer_23 (
    .in0({6{1'b0}}), .in1(6'b010111), .out(srli), .sel(and_23_out));
  Multiplexer #(.width(6), .enable("false")) multiplexer_24 (
    .in0({6{1'b0}}), .in1(6'b011000), .out(ori), .sel(and_24_out));
  Multiplexer #(.width(6), .enable("false")) multiplexer_25 (
    .in0({6{1'b0}}), .in1(6'b011001), .out(andi), .sel(and_25_out));
  Comparator #(.width(7), .mode("unsigned")) comparator_66 (
    .a(in_1[6:0]), .b(7'b0100011), .eq(comparator_66_eq));  // open: gt, lt
  Comparator #(.width(3), .mode("unsigned")) comparator_67 (
    .a(in_1[14:12]), .b(3'b010), .eq(comparator_67_eq));  // open: gt, lt
  Comparator #(.width(7), .mode("unsigned")) comparator_68 (
    .a(in_1[6:0]), .b(7'b1100011), .eq(comparator_68_eq));  // open: gt, lt
  Comparator #(.width(3), .mode("unsigned")) comparator_69 (
    .a(in_1[14:12]), .b(3'b000), .eq(comparator_69_eq));  // open: gt, lt
  Comparator #(.width(7), .mode("unsigned")) comparator_70 (
    .a(in_1[6:0]), .b(7'b1100011), .eq(comparator_70_eq));  // open: gt, lt
  Comparator #(.width(3), .mode("unsigned")) comparator_71 (
    .a(in_1[14:12]), .b(3'b100), .eq(comparator_71_eq));  // open: gt, lt
  Comparator #(.width(7), .mode("unsigned")) comparator_72 (
    .a(in_1[6:0]), .b(7'b1100011), .eq(comparator_72_eq));  // open: gt, lt
  Comparator #(.width(3), .mode("unsigned")) comparator_73 (
    .a(in_1[14:12]), .b(3'b110), .eq(comparator_73_eq));  // open: gt, lt
  Comparator #(.width(7), .mode("unsigned")) comparator_74 (
    .a(in_1[6:0]), .b(7'b1100011), .eq(comparator_74_eq));  // open: gt, lt
  Comparator #(.width(3), .mode("unsigned")) comparator_75 (
    .a(in_1[14:12]), .b(3'b001), .eq(comparator_75_eq));  // open: gt, lt
  Comparator #(.width(7), .mode("unsigned")) comparator_76 (
    .a(in_1[6:0]), .b(7'b1100011), .eq(comparator_76_eq));  // open: gt, lt
  Comparator #(.width(3), .mode("unsigned")) comparator_77 (
    .a(in_1[14:12]), .b(3'b111), .eq(comparator_77_eq));  // open: gt, lt
  Comparator #(.width(7), .mode("unsigned")) comparator_78 (
    .a(in_1[6:0]), .b(7'b0010111), .eq(comparator_78_eq));  // open: gt, lt
  Comparator #(.width(7), .mode("unsigned")) comparator_79 (
    .a(in_1[6:0]), .b(7'b0110111), .eq(comparator_79_eq));  // open: gt, lt
  Comparator #(.width(7), .mode("unsigned")) comparator_80 (
    .a(in_1[6:0]), .b(7'b1101111), .eq(comparator_80_eq));  // open: gt, lt
  Comparator #(.width(7), .mode("unsigned")) comparator_81 (
    .a(in_1[6:0]), .b(7'b1100111), .eq(comparator_81_eq));  // open: gt, lt
  Comparator #(.width(3), .mode("unsigned")) comparator_82 (
    .a(in_1[14:12]), .b(3'b000), .eq(comparator_82_eq));  // open: gt, lt
  Comparator #(.width(3), .mode("unsigned")) comparator_83 (
    .a(in_1[14:12]), .b(3'b110), .eq(comparator_83_eq));  // open: gt, lt
  Comparator #(.width(3), .mode("unsigned")) comparator_84 (
    .a(in_1[14:12]), .b(3'b111), .eq(comparator_84_eq));  // open: gt, lt
  and and_26 (and_26_out, comparator_66_eq, comparator_67_eq);
  not not_1 (not_1_out, in_2);
  not not_2 (not_2_out, in_3);
  not not_3 (not_3_out, in_3);
  and and_27 (and_27_out, comparator_81_eq, comparator_82_eq);
  or or_1 (out_4, comparator_83_eq, comparator_84_eq);
  Multiplexer #(.width(6), .enable("false")) multiplexer_26 (
    .in0({6{1'b0}}), .in1(6'b011010), .out(sw), .sel(and_26_out));
  Multiplexer #(.width(6), .enable("false")) multiplexer_27 (
    .in0({6{1'b0}}), .in1(6'b011011), .out(beq), .sel(and_28_out));
  and and_28 (and_28_out, comparator_68_eq, not_1_out, comparator_69_eq);
  Multiplexer #(.width(6), .enable("false")) multiplexer_28 (
    .in0({6{1'b0}}), .in1(6'b011101), .out(blt), .sel(and_29_out));
  and and_29 (and_29_out, comparator_70_eq, not_2_out, comparator_71_eq);
  Multiplexer #(.width(6), .enable("false")) multiplexer_29 (
    .in0({6{1'b0}}), .in1(6'b011111), .out(bltu), .sel(and_30_out));
  and and_30 (and_30_out, comparator_72_eq, not_3_out, comparator_73_eq);
  Multiplexer #(.width(6), .enable("false")) multiplexer_30 (
    .in0({6{1'b0}}), .in1(6'b100001), .out(bne), .sel(and_31_out));
  and and_31 (and_31_out, comparator_74_eq, in_2, comparator_75_eq);
  Multiplexer #(.width(6), .enable("false")) multiplexer_31 (
    .in0({6{1'b0}}), .in1(6'b100011), .out(bgeu), .sel(and_32_out));
  and and_32 (and_32_out, comparator_76_eq, in_3, comparator_77_eq);
  Multiplexer #(.width(6), .enable("false")) multiplexer_32 (
    .in0({6{1'b0}}), .in1(6'b100101), .out(auipc), .sel(comparator_78_eq));
  Multiplexer #(.width(6), .enable("false")) multiplexer_33 (
    .in0({6{1'b0}}), .in1(6'b100110), .out(lui), .sel(comparator_79_eq));
  Multiplexer #(.width(6), .enable("false")) multiplexer_34 (
    .in0({6{1'b0}}), .in1(6'b100111), .out(jal), .sel(comparator_80_eq));
  Multiplexer #(.width(6), .enable("false")) multiplexer_35 (
    .in0({6{1'b0}}), .in1(6'b101000), .out(jalr), .sel(and_27_out));
  Comparator #(.width(7), .mode("unsigned")) comparator_85 (
    .a(in_1[6:0]), .b(7'b1100011), .eq(comparator_85_eq));  // open: gt, lt
  Comparator #(.width(3), .mode("unsigned")) comparator_86 (
    .a(in_1[14:12]), .b(3'b000), .eq(comparator_86_eq));  // open: gt, lt
  Comparator #(.width(7), .mode("unsigned")) comparator_87 (
    .a(in_1[6:0]), .b(7'b1100011), .eq(comparator_87_eq));  // open: gt, lt
  Comparator #(.width(3), .mode("unsigned")) comparator_88 (
    .a(in_1[14:12]), .b(3'b100), .eq(comparator_88_eq));  // open: gt, lt
  Comparator #(.width(7), .mode("unsigned")) comparator_89 (
    .a(in_1[6:0]), .b(7'b1100011), .eq(comparator_89_eq));  // open: gt, lt
  Comparator #(.width(3), .mode("unsigned")) comparator_90 (
    .a(in_1[14:12]), .b(3'b110), .eq(comparator_90_eq));  // open: gt, lt
  Comparator #(.width(7), .mode("unsigned")) comparator_91 (
    .a(in_1[6:0]), .b(7'b1100011), .eq(comparator_91_eq));  // open: gt, lt
  Comparator #(.width(3), .mode("unsigned")) comparator_92 (
    .a(in_1[14:12]), .b(3'b001), .eq(comparator_92_eq));  // open: gt, lt
  Comparator #(.width(7), .mode("unsigned")) comparator_93 (
    .a(in_1[6:0]), .b(7'b1100011), .eq(comparator_93_eq));  // open: gt, lt
  Comparator #(.width(3), .mode("unsigned")) comparator_94 (
    .a(in_1[14:12]), .b(3'b111), .eq(comparator_94_eq));  // open: gt, lt
  not not_4 (not_4_out, in_2);
  and and_33 (and_33_out, comparator_85_eq, in_2, comparator_86_eq);
  and and_34 (and_34_out, comparator_87_eq, in_3, comparator_88_eq);
  and and_35 (and_35_out, comparator_89_eq, in_3, comparator_90_eq);
  and and_36 (and_36_out, comparator_91_eq, not_4_out, comparator_92_eq);
  and and_37 (and_37_out, comparator_93_eq, in_3, comparator_94_eq);
  Multiplexer #(.width(6), .enable("false")) multiplexer_36 (
    .in0({6{1'b0}}), .in1(6'b011100), .out(beq2), .sel(and_33_out));
  Multiplexer #(.width(6), .enable("false")) multiplexer_37 (
    .in0({6{1'b0}}), .in1(6'b011110), .out(blt2), .sel(and_34_out));
  Multiplexer #(.width(6), .enable("false")) multiplexer_38 (
    .in0({6{1'b0}}), .in1(6'b100000), .out(bltu2), .sel(and_35_out));
  Multiplexer #(.width(6), .enable("false")) multiplexer_39 (
    .in0({6{1'b0}}), .in1(6'b100010), .out(bne2), .sel(and_36_out));
  Multiplexer #(.width(6), .enable("false")) multiplexer_40 (
    .in0({6{1'b0}}), .in1(6'b100100), .out(bgeu2), .sel(and_37_out));
  ROM #(.addrWidth(6), .dataWidth(18)) rom_1 (
    .addr(or_2_out),
    .data({out_6, out_5, rom_1_data[13], out_7, out_8, rom_1_data[9:7], out_11, out_12, out_9}));
  assign or_2_out = bgeu2 | add | mul | sub | sll_541af34d | mulh | mulhu | xor_aa50a71f | div | divu | srl_c9755298 | or_13e46807 | remu | and_c641ead7 | sw | beq | blt | bltu | bne | bgeu | auipc | lui | jal | jalr | beq2 | blt2 | bltu2 | bne2;  // OR_Gate or_2, 6 bits wide
  or or_3 (out_10, rom_1_data[7], rom_1_data[8], rom_1_data[9]);

  // Other names for the same wires on the sheet: BrEq = in_2; BrLT = in_3; INSTRUCTION[31:0] = in_1;
  //   opcode[6:0] = in_1[6:0]; funct3[2:0] = in_1[14:12]; funct7[6:0] = in_1[31:25]

  // Notes on the sheet:
  //   R-TYPE
  //   I-TYPE
  //   SB-TYPE
  //   contents of rom_1 (hex, n*v repeats v):
  //   0 d3 d5 d4 df d7 d6 d2 d9 d8 db d1 da d0 543 5c3 4c3 643 6c3 4d3 4df 4dd 4d2 4db 4d1 4d0 4403 8c83
  //   28c83 8c83 28c83 ac83 2ac83 8c83 28c83 ac83 2ac83 ccd3 d4d3 30ce3 204e3
endmodule
